# Fritzing sketch GeigerCounter (saved by Fritzing 0.9.4)
breadboards: 1

parts:
  WeMos_D1_Mini1 = WeMos D1 Mini  # not connected
  Q4 = NPN-Transistor [package="TO92 [THT]"]
  C1 = Ceramic Capacitor [capacitance=1nF package="100 mil [THT, multilayer]"]
  R1 = Resistor [tolerance=±5% resistance=4.7k package="2512 [SMD]"]  # not connected
  R2 = Resistor [tolerance=±5% resistance=4.7k package="2512 [SMD]"]  # not connected

nets:
  N1: Q4.B, C1.0

notes:
  NPN Mosfet S G D
