# Fritzing sketch sensorclock (saved by Fritzing 0.9.4)
breadboards: 1

parts:
  Part1 = Adafruit Feather HUZZAH ESP8266 [part_number="Adafruit #2821"]
  Part2 = 0.56" 7-segment LED Backpack [part_number=881]
  Part3 = OLED Monochrome 128x64 0.96 inch [part_number=326]
  DHT1 = DHT22 Humidity and Temperature Sensor
  Part4 = Adafruit BMP085 [part_number="Adafruit #391"]
  Part5 = Adafruit CCS811  # not connected
  Part6 = Adafruit TSL2561 [part_number="Adafruit #439"]  # not connected

nets:
  GND: Part1.GND, Part3.GND
  3.3V: Part1.3.3V, Part3.3.3V
  N1: Part1.GPIO0, DHT1.DATA
  N2: Part1.GPIO5/SCL, Part3.SCLK_SCK
  N3: Part1.GPIO4/SDA, Part3.DC_SA0
  N4: Part2.SCL, Part4.GND

custom parts:
  Adafruit Feather HUZZAH ESP8266: his is the Adafruit Feather HUZZAH ESP8266 - our take on an 'all-in-one' ESP8266 WiFi development board with built in USB and battery charging. Its an ESP8266 WiFi module with all the extras you need, ready to rock! We have other boards in the Feather family, check'em out here. At the Feather HUZZAH's heart is an ESP8266 WiFi microcontroller clocked at 80 MHz and at 3.3V logic. This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
  0.56" 7-segment LED Backpack: This 0.56" 7-segment LED display includes a driver chip for simple control via an I2C interface. The backpack features address-selection jumpers so you can connect up to eight displays on a single I2C bus.
  OLED Monochrome 128x64 0.96 inch: These displays are small, only about 1" diameter, but very readable due to the high contrast of an OLED display. This display is made of 128x64 individual white OLED pixels, each one is turned on or off by the controller chip. Because the display makes its own light, no backlight is required. This reduces the power required to run the OLED and is why the display has such high contrast; we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
  Adafruit BMP085: This precision sensor from Bosch is the best low-cost sensing solution for measuring barometric pressure and temperature. Because pressure changes with altitude you can also use it as an altimeter! The sensor is soldered onto a PCB with a 3.3V regulator, I2C level shifter and pull-up resistors on the I2C pins. NEW! We now have a fully 5V compliant version of this board - a 3.3V regulator and a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
  Adafruit TSL2561: The TSL2561 luminosity sensor is an advanced digital light sensor, ideal for use in a wide range of light situations. Compared to low cost CdS cells, this sensor is more precise, allowing for exact lux calculations and can be configured for different gain/timing ranges to detect light ranges from up to 0.1 - 40,000+ Lux on the fly. The best part of this sensor is that it contains both infrared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
